# Fritzing sketch Breadboard (saved by Fritzing 0.8.7b)
breadboards: 1

parts:
  Teensy_3_1 = Teensy 3.1
  LED1 = LED - 5mm [color="Red (633nm)" package="5 mm [THT]"]
  R1 = Resistor [tolerance=±5% resistance=220 package=THT]
  S1 = Toggle Switch [package=THT]
  R2 = Resistor [tolerance=±5% resistance=220 package=THT]
  Part1 = Triple Axis Accelerometer Breakout - ADXL345

nets:
  3V3: Teensy_3_1.3V3, Part1.VCC
  GND: Teensy_3_1.GND, Part1.GND
  N1: LED1.anode, R1.Pin_1
  N2: S1.COM, R2.Pin_1
